# Fritzing sketch shema (saved by Fritzing 0.9.3b)
breadboards: 3

parts:
  Mod1 = Raspberry Pi Pico
  S1 = Microswitch SPDT Endstop [package=THT]
  S2 = Microswitch SPDT Endstop [package=THT]
  R1 = Resistor [tolerance=±5% resistance=220 package="2010 [SMD]"]
  R2 = Resistor [tolerance=±5% resistance=220 package="2512 [SMD]"]
  L2 = Solenoid
  VCC1 = Battery
  Q1 = TIP120 Hi-Current Darlington Transistor
  Q2 = TIP120 Hi-Current Darlington Transistor
  R3 = Resistor [tolerance=±5% resistance=220 package="2010 [SMD]"]
  L1 = Solenoid
  R4 = Resistor [tolerance=±5% resistance=220 package="2010 [SMD]"]
  Matrix_keypad1 = KEYPAD 4x4
  R5 = Resistor [tolerance=±5% resistance=220 package="2512 [SMD]"]
  R6 = Resistor [tolerance=±5% resistance=220 package="2512 [SMD]"]
  R7 = Resistor [tolerance=±5% resistance=220 package="2512 [SMD]"]
  R8 = Resistor [tolerance=±5% resistance=220 package="2512 [SMD]"]
  R9 = Resistor [tolerance=±5% resistance=220 package="2512 [SMD]"]
  R10 = Resistor [tolerance=±5% resistance=220 package="2512 [SMD]"]
  R11 = Resistor [tolerance=±5% resistance=220 package="2512 [SMD]"]
  R12 = Resistor [tolerance=±5% resistance=220 package="2512 [SMD]"]
  LED1 = LED - 3mm [color="Red (633nm)" package="3 mm [THT]"]
  LED2 = LED - 3mm [color="Red (633nm)" package="3 mm [THT]"]
  LED3 = LED - 3mm [color="Red (633nm)" package="3 mm [THT]"]
  R13 = Resistor [tolerance=±5% resistance=220 package="2512 [SMD]"]
  R14 = Resistor [tolerance=±5% resistance=220 package="2512 [SMD]"]
  R15 = Resistor [tolerance=±5% resistance=220 package="2512 [SMD]"]
  Part1 = TFT 2.8 inch 320x240 Touch w microSD [part_number=1770]

nets:
  N1: Mod1.pin_1, R9.Pin_1
  N2: Mod1.pin_2, R10.Pin_1
  N3: Mod1.pin_3, Mod1.pin_18, Mod1.pin_33, Mod1.pin_38, Mod1.pin_42, VCC1.-, Q1.EMITTER, LED1.anode, LED2.anode, LED3.anode, Part1.GND
  N4: Mod1.pin_4, R11.Pin_1
  N5: Mod1.pin_5, R12.Pin_1
  N6: Mod1.pin_6, R3.Pin_0
  N7: Mod1.pin_7, R4.Pin_0
  N8: Mod1.pin_10, Mod1.pin_12, R1.Pin_1
  N9: Mod1.pin_14, R2.Pin_1
  N10: Mod1.pin_16, R13.Pin_0
  N11: Mod1.pin_17, R14.Pin_0
  N12: Mod1.pin_19, R15.Pin_0
  N13: Mod1.pin_20, Part1.LCD_DC
  N14: Mod1.pin_21, Part1.MISO
  N15: Mod1.pin_22, Part1.LCD_CS
  N16: Mod1.pin_24, Part1.SCLK
  N17: Mod1.pin_25, Part1.MOSI
  N18: Mod1.pin_26, Part1.LCD_RST
  N19: Mod1.pin_27, R5.Pin_1
  N20: Mod1.pin_29, R6.Pin_1
  N21: Mod1.pin_31, R7.Pin_1
  N22: Mod1.pin_32, R8.Pin_1
  N23: Mod1.pin_36, S2.C, Part1.+5V
  N24: Mod1.pin_37, S1.C
  N25: S1.NC, R2.Pin_0
  N26: S2.NC, R1.Pin_0
  N27: L2.pin1, Q2.COLLECTOR
  N28: Q1.BASE, R3.Pin_1
  N29: Q1.COLLECTOR, L1.pin1
  N30: Q2.BASE, R4.Pin_1
  N31: Matrix_keypad1.col1, R5.Pin_0
  N32: Matrix_keypad1.col2, R6.Pin_0
  N33: Matrix_keypad1.col3, R7.Pin_0
  N34: Matrix_keypad1.col4, R8.Pin_0
  N35: Matrix_keypad1.row1, R9.Pin_0
  N36: Matrix_keypad1.row2, R10.Pin_0
  N37: Matrix_keypad1.row3, R11.Pin_0
  N38: Matrix_keypad1.row4, R12.Pin_0
  N39: LED1.cathode, R13.Pin_1
  N40: LED2.cathode, R14.Pin_1
  N41: LED3.cathode, R15.Pin_1

notes:
  picoETF resistors
  12V
  microswitches
  solenoids
  leds/products

custom parts:
  Raspberry Pi Pico: Raspberry Pi Pico. Based around the RP2040 microcontroller the Pico is a low cost microcontroller device bringing Raspberry Pi quality, cost, and easy of use to the microcontroller space. Jan 2021, Split part in to two versions: tht (this one) and SMD. This one will drill holes for a .1 in header in pcb to allow plugging in the module as well as providing pads to solder the module to the top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
  Microswitch SPDT Endstop: Microswitch SPDT end stop
  KEYPAD 4x4: Matrix keypad 16 buttons, 4 rows x 4 columns
  TFT 2.8 inch 320x240 Touch w microSD: This TFT display is big (2.8" diagonal) bright (4 white-LED backlight) and colorful! 240x320 pixels with individual RGB pixel control. As a bonus, this display has a resistive touchscreen attached to it already, so you can detect finger presses anywhere on the screen.
